// Logisim project ALU_circuit (1).circ as structural Verilog: 1 circuit, main circuit main
// Z
module main (
  input  A4,
  input  A3,
  input  A2,
  input  A1,
  input  B4,
  input  B3,
  input  B2,
  input  B1,
  input  Cs2,
  input  Cs1,
  input  Cs0_Cin,
  output Z,
  output S,
  output C,
  output V,
  output out_16,
  output out_17,
  output out_18,
  output out_19
);

  wire n7404_1_p2, n7404_1_p4, n7404_1_p6, n7404_1_p9, n7404_1_p11, n7404_1_p12, n7404_1_p13, n7404_1_p14,
       n7408_1_p2, n7408_1_p3, n7408_1_p6, n7408_1_p11, n7408_1_p14, n7408_2_p1, n7408_2_p2, n7408_2_p6,
       n7408_2_p11, n7408_2_p12, n7408_2_p13, n7408_3_p3, n7408_3_p6, n7408_3_p11, n7408_3_p14, n7408_4_p3,
       n7408_4_p9, n7408_4_p13, n7408_4_p14, n7408_5_p2, n7408_5_p3, n7408_5_p5, n7408_5_p6, n7408_5_p11,
       n7408_5_p14, n7432_1_p6, n7432_1_p11, n7432_1_p14, n7432_2_p3, n7432_2_p6, n7432_2_p11, n7432_2_p14,
       n7432_3_p6, n7432_3_p11, n7432_3_p14, n7486_1_p1, n7486_1_p3, n7486_1_p6, n7486_1_p11, n7486_1_p14;

  // _7408 7408_1: pin names not known; wires that end beside it: B1, n7408_1_p2, n7408_1_p3, n7408_1_p3, A1, n7408_1_p6, 1'b0, 1'b1, B2, A2, n7408_1_p11, n7408_1_p11, n7408_1_p2, n7408_1_p14
  // _7404 7404_1: pin names not known; wires that end beside it: Cs0_Cin, n7404_1_p2, Cs1, n7404_1_p4, Cs2, n7404_1_p6, 1'b0, 1'b1, n7404_1_p9, n7408_1_p2, n7404_1_p11, n7404_1_p12, n7404_1_p13, n7404_1_p14
  // _7486 7486_1: pin names not known; wires that end beside it: n7486_1_p1, A1, n7486_1_p3, n7486_1_p1, A2, n7486_1_p6, 1'b0, 1'b1, n7486_1_p1, A3, n7486_1_p11, A4, n7486_1_p1, n7486_1_p14
  // _7408 7408_2: pin names not known; wires that end beside it: n7408_2_p1, n7408_2_p2, Z, n7404_1_p12, Cs0_Cin, n7408_2_p6, 1'b0, 1'b0, n7404_1_p2, Cs1, n7408_2_p11, n7408_2_p12, n7408_2_p13, V
  // _7432 7432_1: pin names not known; wires that end beside it: Cs2, Cs1, n7404_1_p11, n7404_1_p6, n7404_1_p4, n7432_1_p6, 1'b0, 1'b1, n7432_1_p6, n7404_1_p2, n7432_1_p11, Cs2, Cs1, n7432_1_p14
  // _7408 7408_3: pin names not known; wires that end beside it: n7404_1_p6, B1, n7408_3_p3, n7404_1_p6, B2, n7408_3_p6, 1'b0, 1'b1, n7404_1_p6, B4, n7408_3_p11, n7404_1_p6, B3, n7408_3_p14
  // _7408 7408_4: pin names not known; wires that end beside it: n7404_1_p11, n7404_1_p2, n7408_4_p3, Cs2, n7404_1_p4, n7486_1_p1, 1'b0, 1'b1, n7408_4_p9, n7408_2_p13, C, n7404_1_p9, n7408_4_p13, n7408_4_p14
  // _7432 7432_2: pin names not known; wires that end beside it: n7408_3_p3, n7408_4_p3, n7432_2_p3, n7408_3_p6, n7408_4_p3, n7432_2_p6, 1'b0, 1'b1, n7408_4_p3, n7408_3_p11, n7432_2_p11, n7408_4_p3, n7408_3_p14, n7432_2_p14
  // _7408 7408_5: pin names not known; wires that end beside it: n7486_1_p3, n7408_5_p2, n7408_5_p3, n7486_1_p6, n7408_5_p5, n7408_5_p6, 1'b0, 1'b1, n7408_5_p2, n7404_1_p14, n7408_5_p11, n7432_2_p6, n7408_5_p5, n7408_5_p14
  // _7486 7486_2: pin names not known; wires that end beside it: n7432_1_p11, n7432_2_p3, n7404_1_p13, n7408_4_p9, n7408_4_p14, n7408_2_p12, 1'b0, 1'b0
  // _7432 7432_3: pin names not known; wires that end beside it: n7432_1_p14, n7404_1_p2, n7404_1_p9, out_16, out_17, n7432_3_p6, 1'b0, 1'b1, out_19, out_18, n7432_3_p11, n7408_2_p11, n7408_2_p6, n7432_3_p14
  // _7483 7483_1: pin names not known; wires that end beside it: 1'b1, out_17, n7486_1_p11, n7432_2_p14, 1'b1, out_18, n7408_5_p14, n7408_5_p6, 1'b0, n7408_4_p13, n7404_1_p2, 1'b0, n7408_5_p11, n7408_5_p3, out_19
  // _7404 7404_2: pin names not known; wires that end beside it: n7408_1_p6, n7408_5_p2, n7408_1_p14, n7408_5_p5, n7432_3_p11, n7408_2_p2, 1'b0, 1'b1, n7432_3_p6, n7408_2_p1, n7432_3_p14, n7408_2_p13
  // _7483 7483_2: pin names not known; wires that end beside it: n7486_1_p14, 1'b1, 1'b0, 1'b1, 1'b0, 1'b1, n7432_2_p11, out_16, n7408_4_p9, n7408_4_p14, 1'b0, 1'b0, 1'b1

  assign S = out_16;

  // Notes on the sheet:
  //   Cin' (Z)
  //   X4
  //   X3
  //   X2
  //   X1
  //   Cs0'(Cs1+Cs2)
  //   Cs2+Cs1+Cs0'
  //   Y4
  //   Y3
  //   Y2
  //   Y1
  //   Modified Y1
  //   Cin(prev)
  //   S2    S1    S0    operation
  //   0        0      0      A+B+1
  //   0        0      1     A XOR B
  //   0        1      0  Transfer A
  //   0        1      1       A+B
  //   1        0      0    Complement A
  //   1       0      1    Complement A
  //   1       1      0    
  //   1        1     1        A+1
  //   Transfer A
endmodule
