// Logisim project B1_Group5_ita.circ as structural Verilog: 1 circuit, main circuit main
module main (
  input  A3,
  input  A2,
  input  A1,
  input  A0,
  input  B3,
  input  B2,
  input  B1,
  input  B0,
  input  cs2,
  input  cs1,
  input  cs0,
  output C4,
  output F3,
  output F2,
  output F1,
  output F0,
  output C,
  output S,
  output V,
  output Z
);

  wire n7408_1_p4, n7408_1_p6, n7408_1_p7, n7408_1_p8, n7408_1_p11, n7408_1_p13, n7408_2_p4, n7408_2_p7,
       n7408_2_p8, n7432_1_p4, n7432_1_p6, n7432_1_p10, n7483_1_p2, n7483_1_p5, n7483_1_p10, n7483_1_p12,
       n7483_1_p13, n7483_1_p14, n7486_1_p2, n7486_1_p3, n7486_1_p6, n7486_1_p7, n7486_1_p8, n7486_1_p9,
       n7486_1_p12, n7486_1_p13, n7486_2_p6, n7486_2_p11, n74138_1_p2, n74138_1_p10, n74157_1_p2,
       n74157_1_p6, n74157_2_p2;

  // _7486 7486_1: pin names not known; wires that end beside it: 1'b1, n7486_1_p2, n7486_1_p3, A0, A3, n7486_1_p6, n7486_1_p7, n7486_1_p8, n7486_1_p9, A1, A2, n7486_1_p12, n7486_1_p13, 1'b0
  // _7483 7483_1: pin names not known; wires that end beside it: A1, n7483_1_p2, n7486_1_p8, A0, n7483_1_p5, n7486_1_p2, 1'b1, 1'b0, n7486_1_p9, n7483_1_p10, A2, n7483_1_p12, n7483_1_p13, n7483_1_p14, A3, n7486_1_p3
  // _74157 74157_1: pin names not known; wires that end beside it: 1'b1, n74157_1_p2, 1'b0, B0, B3, n74157_1_p6, n74157_1_p6, n7486_1_p2, n7486_1_p3, B1, B2, n74157_1_p6, n74157_1_p6, n7486_1_p8
  // _74157 74157_2: pin names not known; wires that end beside it: 1'b1, n74157_2_p2, 1'b0, n7486_1_p6, n7486_1_p7, n7483_1_p2, n7483_1_p14, F0, F3, n7486_1_p12, n7486_1_p13, n7483_1_p5, n7483_1_p13, F1, F2, 1'b0
  // _7408 7408_1: pin names not known; wires that end beside it: n7486_1_p9, 1'b0, 1'b1, n7408_1_p4, n7483_1_p10, n7408_1_p6, n7408_1_p7, n7408_1_p8, n74157_1_p2, n7408_1_p8, n7408_1_p11, n7408_1_p11, n7408_1_p13, n74157_2_p2, n7408_1_p7, 1'b0
  // _7432 7432_1: pin names not known; wires that end beside it: 1'b1, F0, F1, n7432_1_p4, n7432_1_p4, n7432_1_p6, F2, F3, n7432_1_p6, n7432_1_p10, 1'b0
  // _74138 74138_1: pin names not known; wires that end beside it: 1'b0, n74138_1_p2, n74157_1_p6, n7408_1_p4, 1'b1, n7408_1_p6, 1'b0, n7483_1_p10, 1'b0, n74138_1_p10, cs2, n7408_1_p11, cs1, n7408_1_p13, cs0, 1'b1
  // _7408 7408_2: pin names not known; wires that end beside it: 1'b1, n7483_1_p12, n74138_1_p10, n7408_2_p4, n7408_1_p11, C, n7408_2_p7, n7408_2_p8, n7408_2_p7, n7408_2_p4, n74138_1_p2, V, n7408_2_p4, 1'b0
  // _7486 7486_2: pin names not known; wires that end beside it: 1'b1, n7483_1_p14, n7432_1_p10, A3, 1'b1, n7486_2_p6, Z, n7486_2_p6, n7483_1_p12, n7486_1_p3, n7486_2_p11, n7486_2_p11, n7408_2_p8, 1'b0

  assign C4 = C;
  assign S = F3;

  // Notes on the sheet:
  //   S2    S1    S0    operation
  //   0        0      0     A+B+1
  //   0        0      1     A XOR B
  //   0        1      0     Transfer A
  //   0        1      1     A+B
  //   1        0      0     Complement A
  //   1        0      1     Complement A
  //   1        1      0     Transfer A
  //   1        1      1     A+1
  //   P3
  //   P0
  //   P2
  //   P1
  //   P4
endmodule
