// Logisim project old_design.circ as structural Verilog: 1 circuit, main circuit main
// Z
module main (
  input  A3,
  input  A2,
  input  A1,
  input  A0,
  input  B3,
  input  B2,
  input  B1,
  input  B0,
  input  Cs2,
  input  Cs1,
  input  Cs0_Cin,
  output V,
  output Z,
  output S,
  output C,
  output O3,
  output O2,
  output O1,
  output O0
);

  wire add2_p4, and1_p7, and1_p8, and1_p13, and1_p15, and2_p7, and2_p8, and2_p12, and2_p14, and3_p11,
       and3_p12, and3_p17, and3_p18, and4_p10, and4_p11, and4_p16, not1_p3, not1_p4, not1_p6, not1_p8,
       not1_p9, not1_p13, or1_p7, or1_p9, or1_p15, or2_p4, or2_p7, or3_p8, or3_p11, xor1_p4, xor1_p6,
       xor2_p1, xor2_p12, xor2_p18, xor2_p19;

  // _7486 xor1: pin names not known; wires that end beside it: 1'b1, Cs1, Cs0_Cin, xor1_p4, C, xor1_p6, V, 1'b0
  // _7404 not1: pin names not known; wires that end beside it: 1'b1, Cs2, not1_p3, not1_p4, not1_p4, not1_p6, Cs1, not1_p8, not1_p9, not1_p9, Z, Cs0_Cin, not1_p13, not1_p13
  // _7408 and2: pin names not known; wires that end beside it: not1_p6, 1'b1, B0, B2, Cs0_Cin, Cs0_Cin, and2_p7, and2_p8, B1, Cs0_Cin, Cs0_Cin, and2_p12, B3, and2_p14
  // _7408 and3: pin names not known; wires that end beside it: and2_p8, and2_p12, 1'b0, and2_p14, and2_p7, 1'b1, not1_p6, not1_p6, B0, B2, and3_p11, and3_p12, B1, B3, not1_p6, not1_p6, and3_p17, and3_p18, 1'b0
  // _7408 and1: pin names not known; wires that end beside it: 1'b0, 1'b1, Cs2, not1_p4, Cs1, not1_p9, and1_p7, and1_p8, and1_p7, and1_p8, Cs0_Cin, not1_p13, and1_p13, and1_p13, and1_p15, 1'b0
  // _7432 or1: pin names not known; wires that end beside it: and1_p15, 1'b1, and1_p13, and2_p7, and1_p15, Cs2, or1_p7, or1_p7, or1_p9, xor1_p4, Cs2, Cs2, and2_p14, not1_p3, or1_p15, 1'b0
  // _7432 or3: pin names not known; wires that end beside it: and3_p18, and3_p12, and3_p17, and3_p11, 1'b1, and2_p8, Cs2, or3_p8, and2_p12, Cs2, or3_p11, 1'b0
  // _7408 and4: pin names not known; wires that end beside it: or3_p11, or3_p8, or1_p15, or1_p9, 1'b1, or1_p15, or3_p8, not1_p9, not1_p9, and4_p10, and4_p11, or1_p9, or3_p11, not1_p9, not1_p9, and4_p16
  // _7483 add2: pin names not known; wires that end beside it: 1'b0, O3, 1'b0, add2_p4, C, and3_p18, 1'b1, 1'b0, 1'b0, xor1_p6, 1'b0, 1'b0, 1'b0
  // _7432 or2: pin names not known; wires that end beside it: 1'b1, O0, O1, or2_p4, O3, or2_p4, or2_p7, O2, not1_p8, or2_p7, 1'b0
  // _7486 xor2: pin names not known; wires that end beside it: xor2_p1, xor2_p1, 1'b0, and4_p11, and4_p10, and4_p16, 1'b1, and4_p10, A3, A1, xor2_p1, xor2_p12, add2_p4, and4_p16, and4_p11, A0, A2, xor2_p18, xor2_p19, 1'b0, A3, A2, A1, A0, add2_p4, xor2_p19, xor2_p12
  // _7483 add1: pin names not known; wires that end beside it: xor2_p18, xor2_p12, O0, and3_p17, xor2_p18, O1, and3_p11, 1'b1, 1'b0, and3_p12, or1_p7, xor2_p19, O2, xor1_p6, 1'b0, 1'b0, xor1_p6, 1'b1

  assign S = O3;

  // Notes on the sheet:
  //   S0
  //   (S2 + (S1 xor s0))'
  //   s2' s1' s0'
  //   S0. B3B2B1B0
  //   s2.s1.s0
  //   Y3Y2Y1Y0
  //   s2'.s1'.s0'
  //   Z
  //   BiS0 + S2
  //   S1'(BiS0+S2)
  //   X3X2X1X0
  //   C3 / S2
  //   S2    S1    S0    operation
  //   0        0      0     A+B+1
  //   0        0      1     A XOR B
  //   0        1      0     Transfer A
  //   0        1      1     A+B
  //   1        0      0     Complement A
  //   1        0      1     Complement A
  //   1        1      0     Transfer A
  //   1        1      1     A+1
endmodule
