// Logisim project My_4_bit_mips.circ as structural Verilog: 7 circuits, main circuit main
module main (
  output [3:0] sp,
  output [3:0] t4,
  output [3:0] t3,
  output [3:0] t2,
  output [3:0] t1,
  output [3:0] t0,
  output [3:0] zero
);

  wire ALU_zero_flag, CLK_out, control_unit_1_alusrc, control_unit_1_brancheq, control_unit_1_branchnoteq,
       control_unit_1_jump, control_unit_1_memread, control_unit_1_memtoreg, control_unit_1_memwrite,
       control_unit_1_regdst, control_unit_1_regwrite, multiplexer_5_out, Reset_out;
  wire [2:0] control_unit_1_aluop;
  wire [3:0] ALU_output, data_memory_1_data_read, Instruction_Memory_dst_reg_shamt_immdt__0_3,
       Instruction_Memory_opcode__12_15, Instruction_Memory_src_reg_1__8_11,
       Instruction_Memory_src_reg_2__dst_reg__4_7, multiplexer_1_out, multiplexer_3_out, multiplexer_6_out,
       registers_1_read_data2, registers_1_read_data_1;
  wire [7:0] adder_1_out, adder_2_out, bit_extender_1_out, Instruction_Memory_target_jump_address,
       multiplexer_2_out, multiplexer_4_out, PC_current_value;

  // Probe on multiplexer_4_out
  Button Reset (.out(Reset_out));
  Adder adder_1 (.a(PC_current_value), .b(8'h1), .out(adder_1_out));  // open: cin, cout
  // Probe on PC_current_value
  PC PC (.stored_value(multiplexer_4_out), .Clock(CLK_out), .Reset(Reset_out), .Current_value(PC_current_value));
  Clock CLK (.out(CLK_out));
  // Probe on Instruction_Memory_opcode__12_15
  // Probe on Instruction_Memory_src_reg_1__8_11
  // Probe on Instruction_Memory_src_reg_2__dst_reg__4_7
  Instruction_Memory Instruction_Memory (
    .PC_input(PC_current_value), .OpCode__12_15(Instruction_Memory_opcode__12_15),
    .Dst_Reg_Shamt_Immdt__0_3(Instruction_Memory_dst_reg_shamt_immdt__0_3),
    .Src_Reg_2__Dst_Reg__4_7(Instruction_Memory_src_reg_2__dst_reg__4_7),
    .Target_Jump_Address(Instruction_Memory_target_jump_address),
    .Src_Reg_1__8_11(Instruction_Memory_src_reg_1__8_11));
  // Probe on Instruction_Memory_dst_reg_shamt_immdt__0_3
  assign bit_extender_1_out = {{4{Instruction_Memory_dst_reg_shamt_immdt__0_3[3]}}, Instruction_Memory_dst_reg_shamt_immdt__0_3};  // Bit_Extender bit_extender_1
  Control_Unit control_unit_1 (
    .OpCode(Instruction_Memory_opcode__12_15), .RegWrite(control_unit_1_regwrite),
    .ALUSrc(control_unit_1_alusrc), .MemWrite(control_unit_1_memwrite), .ALUOp(control_unit_1_aluop),
    .MemToReg(control_unit_1_memtoreg), .MemRead(control_unit_1_memread), .BranchEq(control_unit_1_brancheq),
    .BranchNotEq(control_unit_1_branchnoteq), .Jump(control_unit_1_jump), .RegDst(control_unit_1_regdst));
  // Probe on control_unit_1_aluop
  Multiplexer #(.width(4), .enable("false")) multiplexer_1 (
    .in0(Instruction_Memory_src_reg_2__dst_reg__4_7), .in1(Instruction_Memory_dst_reg_shamt_immdt__0_3),
    .out(multiplexer_1_out), .sel(control_unit_1_regdst));
  Adder adder_2 (.a(bit_extender_1_out), .b(adder_1_out), .out(adder_2_out));  // open: cin, cout
  Registers registers_1 (
    .RegWrite(control_unit_1_regwrite), .CLK(CLK_out), .Dst_Reg(multiplexer_1_out),
    .WriteData(multiplexer_6_out), .CLR(Reset_out), .Src_Reg1(Instruction_Memory_src_reg_1__8_11),
    .Src_Reg2(Instruction_Memory_src_reg_2__dst_reg__4_7), .zero__t0_4__sp({sp, t4, t3, t2, t1, t0, zero}),
    .Read_Data_1(registers_1_read_data_1), .Read_Data2(registers_1_read_data2));
  // Probe on registers_1_read_data2
  // Probe on Instruction_Memory_dst_reg_shamt_immdt__0_3
  Multiplexer #(.width(8), .enable("false")) multiplexer_2 (
    .in0(adder_1_out), .in1(adder_2_out), .out(multiplexer_2_out), .sel(multiplexer_5_out));
  // Probe on registers_1_read_data2
  Multiplexer #(.width(4), .enable("false")) multiplexer_3 (
    .in0(registers_1_read_data2), .in1(Instruction_Memory_dst_reg_shamt_immdt__0_3), .out(multiplexer_3_out),
    .sel(control_unit_1_alusrc));
  // Probe on multiplexer_3_out
  Multiplexer #(.width(8), .enable("false")) multiplexer_4 (
    .in0(multiplexer_2_out), .in1(Instruction_Memory_target_jump_address), .out(multiplexer_4_out),
    .sel(control_unit_1_jump));
  Multiplexer #(.enable("false")) multiplexer_5 (
    .in0(control_unit_1_branchnoteq), .in1(control_unit_1_brancheq), .out(multiplexer_5_out),
    .sel(ALU_zero_flag));
  // Probe on registers_1_read_data_1
  _4_bit_ALU ALU (
    .A(registers_1_read_data_1), .B(multiplexer_3_out), .Zero_Flag(ALU_zero_flag), .Output(ALU_output),
    .ALUopcode(control_unit_1_aluop));
  // Probe on ALU_output
  // Probe on data_memory_1_data_read
  Data_Memory data_memory_1 (
    .Address(ALU_output), .Write_Data(registers_1_read_data2), .CLR(Reset_out), .CLK(CLK_out),
    .MemWrite(control_unit_1_memwrite), .MemRead(control_unit_1_memread), .Data_Read(data_memory_1_data_read));
  // Probe on multiplexer_6_out
  Multiplexer #(.width(4), .enable("false")) multiplexer_6 (
    .in0(ALU_output), .in1(data_memory_1_data_read), .out(multiplexer_6_out), .sel(control_unit_1_memtoreg));

  // Notes on the sheet:
  //   1
  //   2
  //   1
  //   5
  //   2
  //   6
  //   3
  //   4
endmodule

module PC (
  input  [7:0] stored_value,
  input  Clock,
  input  Reset,
  output [7:0] Current_value
);

  Register #(.trigger("falling"), .Select("low")) register_1 (
    .D(stored_value), .Q(Current_value), .clk(Clock), .clr(Reset));  // open: en
endmodule

module Instruction_Memory (
  input  [7:0] PC_input,
  output [3:0] Dst_Reg_Shamt_Immdt__0_3,
  output [3:0] Src_Reg_2__Dst_Reg__4_7,
  output [7:0] Target_Jump_Address,
  output [3:0] Src_Reg_1__8_11,
  output [3:0] OpCode__12_15
);

  ROM #(.dataWidth(16), .Select("high")) rom_1 (
    .addr(PC_input),
    .data({OpCode__12_15, Src_Reg_1__8_11, Src_Reg_2__Dst_Reg__4_7, Dst_Reg_Shamt_Immdt__0_3}), .sel(1'b1));

  assign Target_Jump_Address = {Src_Reg_1__8_11, Src_Reg_2__Dst_Reg__4_7};

  // Notes on the sheet:
  //   contents of rom_1 (hex, n*v repeats v):
  //   306f 3023 503e 6231 c234 d135 9323 d135 9323 1331 a341 21c0 441 f334 5661 9620 5661 9630 21b0 8131
  //   7531 f630 3661 b352 f620 3661 21c0 e138
endmodule

module _4_bit_ALU (
  input  [3:0] A,
  input  [3:0] B,
  input  [2:0] ALUopcode,
  output Zero_Flag,
  output [3:0] Output
);

  wire [3:0] adder_1_out, and_1_out, nor_1_out, or_1_out, shifter_1_out, shifter_2_out, subtractor_1_out;

  Adder #(.width(4)) adder_1 (.a(A), .b(B), .out(adder_1_out), .cin(1'b0));  // open: cout
  Subtractor #(.width(4)) subtractor_1 (.a(A), .b(B), .out(subtractor_1_out), .bin(1'b0));  // open: bout
  assign or_1_out = A | B;  // OR_Gate or_1, 4 bits wide
  assign and_1_out = A & B;  // AND_Gate and_1, 4 bits wide
  assign nor_1_out = ~(A | B);  // NOR_Gate nor_1, 4 bits wide
  Shifter #(.width(4)) shifter_1 (.in(A), .\dist (B[1:0]), .out(shifter_1_out));
  Shifter #(.width(4), .shift("lr")) shifter_2 (.in(A), .\dist (B[1:0]), .out(shifter_2_out));
  Multiplexer #(.select(3), .width(4), .enable("false")) multiplexer_1 (
    .in0(adder_1_out), .in1(subtractor_1_out), .in2(or_1_out), .in3(and_1_out), .in4(nor_1_out),
    .in5(shifter_1_out), .in6(shifter_2_out), .in7(4'b0000), .out(Output), .sel(ALUopcode));
  nor nor_2 (Zero_Flag, Output[0], Output[1], Output[2], Output[3]);
endmodule

module Data_Memory (
  input  [3:0] Address,
  input  [3:0] Write_Data,
  input  CLR,
  input  CLK,
  input  MemWrite,
  input  MemRead,
  output [3:0] Data_Read
);

  wire not_1_out;

  not not_1 (not_1_out, CLK);
  RAM #(.addrWidth(4), .dataWidth(4), .bus("separate"), .simpleMode("false"), .Select("low")) ram_1 (
    .addr(Address), .din(Write_Data), .data(Data_Read), .str(MemWrite), .clk(not_1_out), .ld(MemRead),
    .clr(CLR));  // open: sel
endmodule

module Registers (
  input  RegWrite,
  input  CLK,
  input  [3:0] Dst_Reg,
  input  [3:0] WriteData,
  input  CLR,
  input  [3:0] Src_Reg1,
  input  [3:0] Src_Reg2,
  output [27:0] zero__t0_4__sp,
  output [3:0] Read_Data_1,
  output [3:0] Read_Data2
);

  wire and_1_out, demultiplexer_1_out1, demultiplexer_1_out2, demultiplexer_1_out3, demultiplexer_1_out4,
       demultiplexer_1_out5, demultiplexer_1_out6, not_1_out, not_2_out, not_3_out, not_4_out, not_5_out,
       not_6_out;

  and and_1 (and_1_out, RegWrite, CLK);
  Demultiplexer #(.select(3), .enable("false")) demultiplexer_1 (
    .out1(demultiplexer_1_out1), .out2(demultiplexer_1_out2), .out3(demultiplexer_1_out3),
    .out4(demultiplexer_1_out4), .out5(demultiplexer_1_out5), .out6(demultiplexer_1_out6), .in(and_1_out),
    .sel(Dst_Reg[2:0]));  // open: out0, out7
  not not_1 (not_1_out, demultiplexer_1_out1);
  not not_2 (not_2_out, demultiplexer_1_out2);
  not not_3 (not_3_out, demultiplexer_1_out3);
  not not_4 (not_4_out, demultiplexer_1_out4);
  not not_5 (not_5_out, demultiplexer_1_out5);
  not not_6 (not_6_out, demultiplexer_1_out6);
  Register #(.width(4), .Select("low")) t0 (
    .D(WriteData), .Q(zero__t0_4__sp[7:4]), .clk(not_1_out), .clr(CLR));  // open: en
  Register #(.width(4), .Select("low")) t1 (
    .D(WriteData), .Q(zero__t0_4__sp[11:8]), .clk(not_2_out), .clr(CLR));  // open: en
  Register #(.width(4), .Select("low")) t2 (
    .D(WriteData), .Q(zero__t0_4__sp[15:12]), .clk(not_3_out), .clr(CLR));  // open: en
  Register #(.width(4), .Select("low")) t3 (
    .D(WriteData), .Q(zero__t0_4__sp[19:16]), .clk(not_4_out), .clr(CLR));  // open: en
  Register #(.width(4), .Select("low")) t4 (
    .D(WriteData), .Q(zero__t0_4__sp[23:20]), .clk(not_5_out), .clr(CLR));  // open: en
  Register #(.width(4), .Select("low")) sp (
    .D(WriteData), .Q(zero__t0_4__sp[27:24]), .clk(not_6_out), .clr(CLR));  // open: en
  Multiplexer #(.select(3), .width(4), .enable("false")) multiplexer_1 (
    .in0(4'b0000), .in1(zero__t0_4__sp[7:4]), .in2(zero__t0_4__sp[11:8]), .in3(zero__t0_4__sp[15:12]),
    .in4(zero__t0_4__sp[19:16]), .in5(zero__t0_4__sp[23:20]), .in6(zero__t0_4__sp[27:24]), .in7(4'b0000),
    .out(Read_Data_1), .sel(Src_Reg1[2:0]));
  Multiplexer #(.select(3), .width(4), .enable("false")) multiplexer_2 (
    .in0(4'b0000), .in1(zero__t0_4__sp[7:4]), .in2(zero__t0_4__sp[11:8]), .in3(zero__t0_4__sp[15:12]),
    .in4(zero__t0_4__sp[19:16]), .in5(zero__t0_4__sp[23:20]), .in6(zero__t0_4__sp[27:24]), .in7(4'b0000),
    .out(Read_Data2), .sel(Src_Reg2[2:0]));

  assign zero__t0_4__sp[3:0] = 4'b0000;

  // Notes on the sheet:
  //   $zero
endmodule

module Control_Unit (
  input  [3:0] OpCode,
  output RegWrite,
  output ALUSrc,
  output MemWrite,
  output [2:0] ALUOp,
  output MemToReg,
  output MemRead,
  output BranchEq,
  output BranchNotEq,
  output Jump,
  output RegDst
);

  ROM #(.addrWidth(4), .dataWidth(12), .Select("low")) rom_1 (
    .addr(OpCode),
    .data({RegDst, Jump, BranchNotEq, BranchEq, MemRead, MemToReg, ALUOp, MemWrite, ALUSrc, RegWrite}));

  // Notes on the sheet:
  //   contents of rom_1 (hex, n*v repeats v):
  //   2b 33 400 3 13 b 801 1b 811 6 108 819 809 821 208 c3
endmodule
